# Fritzing sketch schematic (saved by Fritzing 0.9.3b)
breadboards: 1

parts:
  S1 = SWITCH-MOMENTARY-2 [package=tactile-pth]
  J1 = Piezo Speaker
  LCD1 = LCD screen
  R1 = Resistor [tolerance=±5% resistance=10k package="2010 [SMD]"]
  U1 = LM3480IM4 [package=sot23-3]
  R2 = Resistor [tolerance=±5% resistance=330 package="2010 [SMD]"]
  R3 = Resistor [tolerance=±5% resistance=2k package="2010 [SMD]"]
  part = Electron

nets:
  N1: S1.1, R1.Pin_1, part.WKP, part.B0
  N2: S1.2, part.3V3
  GND: J1.pin1, LCD1.VSS, LCD1.R/W, LCD1.LED-, R1.Pin_0, U1.GND, R3.Pin_1, part.GND
  N3: J1.pin2, part.B2
  N4: LCD1.VDD, U1.OUT, R2.Pin_1
  N5: LCD1.V0, R3.Pin_0
  N6: LCD1.RS, part.D1
  N7: LCD1.E, part.D0
  N8: LCD1.DB4, part.D5
  N9: LCD1.DB5, part.D4
  N10: LCD1.DB6, part.D3
  N11: LCD1.DB7, part.D2
  N12: LCD1.LED+, R2.Pin_0
  N13: U1.IN, part.D7
